// Digital circuit CPU_4.0.dig as structural Verilog
module CPU_4_0 (
  input  clock_IN,
  input  in_2
);

  wire _7448_1_p10, _7448_1_p11, _7448_1_p12, _7448_1_p13, _7448_1_p14, _7448_1_p15, _7448_1_p16,
       _7448_2_p10, _7448_2_p11, _7448_2_p12, _7448_2_p13, _7448_2_p14, _7448_2_p15, _7448_2_p16,
       _74138_1_p9, _74138_1_p10, _74138_1_p11, _74138_1_p12, _74138_1_p13, _74138_1_p14, _74138_1_p15,
       _74138_2_p10, _74138_2_p11, _74138_2_p12, _74138_2_p13, _74154_1_p10, _74154_1_p11, _74154_2_p10,
       _74154_2_p11, _74161_1_p12, _74161_1_p13, _74161_1_p14, _74161_1_p15, _74161_1_p16, _74161_2_p12,
       _74161_2_p13, _74161_2_p14, _74161_2_p15, _74161_2_p16, _74161_3_p12, _74161_3_p13, _74161_3_p14,
       _74161_3_p15, _74161_3_p16, _74161_4_p12, _74161_4_p13, _74161_4_p14, _74161_4_p15, _74245_1_p7,
       _74245_1_p9, _74245_1_p11, _74373_1_p12, _74373_1_p13, _74373_1_p14, _74373_1_p15, _74373_1_p16,
       _74373_1_p17, _74373_1_p18, _74373_1_p19, _74373_2_p14, _74373_2_p15, _74373_2_p16, _74373_2_p17,
       _74373_2_p18, _74373_2_p19, _74373_2_p20, _74373_2_p21, _74373_3_p13, _74373_3_p14, _74373_3_p15,
       _74373_3_p16, _74373_4_p13, _74373_4_p14, _74373_4_p15, _74373_4_p16, _74541_1_p13, _74541_1_p14,
       _74541_1_p15, _74541_1_p16, _74541_1_p17, _74541_1_p18, _74541_1_p19, _74541_1_p20, A0, A1, A2, A3,
       A4, A5, A6, A7, A8, A9, A10, A11, A12, A13, A14, A15, A_2_p13, A_2_p14, A_2_p15, A_2_p16, A_2_p17,
       A_2_p18, A_3_p13, A_3_p14, A_3_p15, A_3_p16, A_3_p17, A_3_p18, A_3_p19, A_3_p20, A_OUT, A_out_2,
       A_WAIT, ADC_EN, ADR_BYTE1, ADR_BYTE2, ALU_A, ALU_q0, ALU_q1, ALU_q2, ALU_q3, ALU_q4, ALU_q5, ALU_q6,
       ALU_q7, and_1_out, and_2_out, and_3_out, and_4_out, and_5_out, and_6_out, and_7_out, and_8_out,
       and_9_out, C_FLAG, CLK, CLK_INSTR, CLK_STACK_AD, CLK_STACK_AU, D0, D1, D2, D3, D4, D5, D6, D7,
       delay_2_out, E_FLAG, eq_JMP, F_I_O, F_LD, F_p15, F_p16, F_p17, F_p18, F_p19, FLAG_CLOCK, FLAG_OUT_EN,
       FLAG_p13, FLAG_p14, FLAG_p15, FLAG_p16, FLAG_p17, FLAG_p18, FLAG_p19, FLAG_p20, G_I_O, G_LD, G_p14,
       G_p15, G_p16, G_p17, G_p18, G_p19, G_p20, G_p21, gt__FLAG, gt_JMP, INSTR_LD, jk_ff_as_1_q, JMP,
       JMP_FC, lt__FLAG, lt_JMP, MINI_CLR, nA_LD, nand_1_out, nDISPLAYFG, nor_2_out, nor_3_out, not_2_out,
       not_3_out, not_4_out, not_5_out, not_6_out, not_7_out, not_8_out, not_19_out, not_20_out,
       nPUSH_POP_AD, nPUSH_POP_AU, nREG_out, nROM_OE, nROM_RAM, O_FLAG, O_nI, OE, or_1_out, or_2_out,
       or_3_out, or_4_out, or_5_out, P_FLAG, PC_BUFFER_2_p13, PC_BUFFER_2_p14, PC_BUFFER_2_p15,
       PC_BUFFER_2_p16, PC_BUFFER_2_p17, PC_BUFFER_2_p18, PC_BUFFER_2_p19, PC_BUFFER_2_p20, PC_BUFFER_p13,
       PC_BUFFER_p14, PC_BUFFER_p15, PC_BUFFER_p16, PC_BUFFER_p17, PC_BUFFER_p18, PC_BUFFER_p19,
       PC_BUFFER_p20, R_out, REG_ADR, REG_in, REG_IN_EN, REG_OUT_EN, reset, S_1, S_2, S_3, SBC_EN,
       switchdt_1_p3, switchdt_2_p3, TO_MEM, WE;
  wire [7:0] eeprom_1_d, eeprom_2_d;
  wire [11:0] INSTR_REG_p30;
  wire [39:0] INSTRUCTION_DECODER_d;

  Button A (.out(A_out_2));
  Button R (.out(R_out));
  // SwitchDT switchdt_1: pin names not known; wires that end beside it: in_2, R_out, switchdt_1_p3
  // SwitchDT switchdt_2: pin names not known; wires that end beside it: clock_IN, A_out_2, switchdt_2_p3
  not not_1 (reset, switchdt_1_p3);
  and and_1 (and_1_out, INSTR_LD, reset);
  not not_2 (not_2_out, CLK_INSTR);
  not not_3 (not_3_out, not_2_out);
  and and_2 (and_2_out, not_4_out, switchdt_2_p3);
  not not_4 (not_4_out, CLK_INSTR);
  or or_1 (or_1_out, not_3_out, not_3_out);
  or or_2 (or_2_out, and_1_out, switchdt_1_p3);
  // _74374 A_2: pin names not known; wires that end beside it: 1'b0, D3, D4, D5, D0, D1, D2, 1'b0, 1'b0, REG_ADR, 1'b1, 1'b0, A_2_p13, A_2_p14, A_2_p15, A_2_p16, A_2_p17, A_2_p18
  or or_3 (or_3_out, or_1_out, and_2_out);
  JK_FF_AS jk_ff_as_1 (
    .Set(1'b0), .J(or_2_out), .C(or_2_out), .K(1'b0), .Clr(jk_ff_as_1_q), .Q(jk_ff_as_1_q));  // open: nQ
  and and_3 (and_3_out, or_3_out, reset);
  and and_4 (and_4_out, reset, MINI_CLR);
  // _74138 _74138_1: pin names not known; wires that end beside it: 1'b1, 1'b0, REG_IN_EN, 1'b0, 1'b0, A_2_p13, A_2_p14, A_2_p15, _74138_1_p9, _74138_1_p10, _74138_1_p11, _74138_1_p12, _74138_1_p13, _74138_1_p14, _74138_1_p15
  // _74138 _74138_2: pin names not known; wires that end beside it: 1'b1, 1'b0, REG_OUT_EN, 1'b0, 1'b0, A_2_p16, A_2_p17, A_2_p18, A_OUT, _74138_2_p10, _74138_2_p11, _74138_2_p12, _74138_2_p13
  Delay delay_1 (.in(_74138_1_p9), .out(nA_LD));
  not not_5 (not_5_out, _74138_1_p10);
  not not_6 (not_6_out, _74138_1_p11);
  not not_7 (not_7_out, _74138_1_p12);
  not not_8 (not_8_out, _74138_1_p13);
  not not_9 (F_LD, _74138_1_p14);
  not not_10 (G_LD, _74138_1_p15);
  _74161 MINI_INSTR_RUN (
    .pin2(1'b0), .pin3(1'b0), .pin4(and_3_out), .pin5(1'b1), .pin6(1'b0), .pin11(INSTR_REG_p30[4]));  // open: pin1, pin7, pin8, pin9, pin10, pin12, pin13, pin14, pin15, pin16
  // _74374 INSTR_REG: pin names not known; wires that end beside it: 1'b0, 1'b0, 1'b1, 1'b1, 1'b1, 1'b0, D0, D1, D2, D3, D4, D5, D6, D7, jk_ff_as_1_q, 1'b1, 1'b0, and_4_out, INSTR_REG_p30[0], INSTR_REG_p30[1], INSTR_REG_p30[2], INSTR_REG_p30[3], INSTR_REG_p30[4], INSTR_REG_p30[5], INSTR_REG_p30[6], INSTR_REG_p30[7], INSTR_REG_p30[8], INSTR_REG_p30[9], INSTR_REG_p30[10], INSTR_REG_p30[11]
  // _74374 B: pin names not known; wires that end beside it: _74138_2_p10, D0, D1, D2, D3, D4, D5, D6, D7, not_5_out, 1'b1, 1'b0, D0, D1, D2, D3, D4, D5, D6, D7
  or or_4 (or_4_out, ALU_A, A_WAIT);
  // _74541 _74541_1: pin names not known; wires that end beside it: nA_LD, nA_LD, D0, D1, D2, D3, D4, D5, D6, D7, 1'b1, 1'b0, _74541_1_p13, _74541_1_p14, _74541_1_p15, _74541_1_p16, _74541_1_p17, _74541_1_p18, _74541_1_p19, _74541_1_p20
  // _74374 C: pin names not known; wires that end beside it: _74138_2_p11, D0, D1, D2, D3, D4, D5, D6, D7, not_6_out, 1'b1, 1'b0, D0, D1, D2, D3, D4, D5, D6, D7
  Delay delay_2 (.in(nA_LD), .out(delay_2_out));
  nand nand_1 (nand_1_out, or_4_out, delay_2_out);
  // _74374 FLAG: pin names not known; wires that end beside it: 1'b0, C_FLAG, O_FLAG, lt__FLAG, E_FLAG, gt__FLAG, P_FLAG, 1'b0, 1'b0, FLAG_CLOCK, 1'b1, 1'b0, FLAG_p13, FLAG_p14, FLAG_p15, FLAG_p16, FLAG_p17, FLAG_p18, FLAG_p19, FLAG_p20
  or or_5 (or_5_out, ADC_EN, SBC_EN);
  // _74374 D: pin names not known; wires that end beside it: _74138_2_p12, D0, D1, D2, D3, D4, D5, D6, D7, not_7_out, 1'b1, 1'b0, D0, D1, D2, D3, D4, D5, D6, D7
  // _74374 A_3: pin names not known; wires that end beside it: 1'b0, _74541_1_p13, _74541_1_p14, _74541_1_p15, _74541_1_p16, _74541_1_p17, _74541_1_p18, _74541_1_p19, _74541_1_p20, nand_1_out, 1'b1, 1'b0, A_3_p13, A_3_p14, A_3_p15, A_3_p16, A_3_p17, A_3_p18, A_3_p19, A_3_p20
  and and_5 (and_5_out, or_5_out, FLAG_p13);
  ROM #(.AddrBits(16), .Bits(40)) INSTRUCTION_DECODER (
    .A({4'b0000, INSTR_REG_p30}), .sel(1'b1),
    .D({INSTRUCTION_DECODER_d[39:37], gt_JMP, eq_JMP, lt_JMP, nDISPLAYFG, TO_MEM, O_nI, INSTRUCTION_DECODER_d[30:29], CLK_INSTR, INSTRUCTION_DECODER_d[27:26], JMP, A_WAIT, SBC_EN, ADC_EN, INSTRUCTION_DECODER_d[21], REG_in, nROM_OE, INSTRUCTION_DECODER_d[18:17], nROM_RAM, CLK_STACK_AD, nPUSH_POP_AD, CLK_STACK_AU, nPUSH_POP_AU, ADR_BYTE2, ADR_BYTE1, S_3, S_2, S_1, REG_IN_EN, REG_OUT_EN, INSTRUCTION_DECODER_d[4], REG_ADR, INSTRUCTION_DECODER_d[2], INSTR_LD, INSTRUCTION_DECODER_d[0]}));
  // _74541 _74541_2: pin names not known; wires that end beside it: FLAG_OUT_EN, FLAG_OUT_EN, FLAG_p13, FLAG_p14, FLAG_p15, FLAG_p16, FLAG_p17, FLAG_p18, FLAG_p19, FLAG_p20, 1'b1, 1'b0, D0, D1, D2, D3, D4, D5, D6, D7
  and and_6 (and_6_out, FLAG_p15, lt_JMP);
  and and_7 (and_7_out, FLAG_p16, eq_JMP);
  and and_8 (and_8_out, FLAG_p17, gt_JMP);
  not not_11 (MINI_CLR, INSTRUCTION_DECODER_d[2]);
  Delay #(.delayTime(2)) delay_3 (.in(INSTRUCTION_DECODER_d[4]), .out(CLK));
  not not_12 (OE, INSTRUCTION_DECODER_d[17]);
  not not_13 (WE, INSTRUCTION_DECODER_d[18]);
  not not_14 (nREG_out, INSTRUCTION_DECODER_d[21]);
  not not_15 (G_I_O, INSTRUCTION_DECODER_d[26]);
  not not_16 (F_I_O, INSTRUCTION_DECODER_d[27]);
  not not_17 (FLAG_OUT_EN, INSTRUCTION_DECODER_d[29]);
  ALU_V2 ALU (
    .CARRY_in(and_5_out), .S_1(S_1), .S_2(S_2), .S_3(S_3), .IN0(A_3_p13), .IN1(A_3_p14), .IN2(A_3_p15),
    .IN3(A_3_p16), .IN4(A_3_p17), .IN5(A_3_p18), .IN6(A_3_p19), .IN7(A_3_p20), .IN8(D0), .IN9(D1), .IN10(D2),
    .IN11(D3), .IN12(D4), .IN13(D5), .IN14(D6), .IN15(D7), .CLOCK(FLAG_CLOCK), .Q0(ALU_q0), .Q1(ALU_q1),
    .Q2(ALU_q2), .Q3(ALU_q3), .Q4(ALU_q4), .Q5(ALU_q5), .Q6(ALU_q6), .Q7(ALU_q7), .P_FLAG(P_FLAG),
    .gt(gt__FLAG), .eq(E_FLAG), .lt(lt__FLAG), .O_FLAG(O_FLAG), .CARRY_FLAG(C_FLAG));
  nor nor_1 (JMP_FC, and_6_out, and_7_out, and_8_out);
  // _74374 E: pin names not known; wires that end beside it: _74138_2_p13, D0, D1, D2, D3, D4, D5, D6, D7, not_8_out, 1'b1, 1'b0, D0, D1, D2, D3, D4, D5, D6, D7
  // _74541 _74541_3: pin names not known; wires that end beside it: A_OUT, A_OUT, A_3_p13, A_3_p14, A_3_p15, A_3_p16, A_3_p17, A_3_p18, A_3_p19, A_3_p20, 1'b1, 1'b0, D0, D1, D2, D3, D4, D5, D6, D7
  // _74374 REG: pin names not known; wires that end beside it: nREG_out, D0, D1, D2, D3, D4, D5, D6, D7, REG_in, 1'b1, 1'b0, D0, D1, D2, D3, D4, D5, D6, D7
  // _74541 _74541_4: pin names not known; wires that end beside it: ALU_A, ALU_A, ALU_q0, ALU_q1, ALU_q2, ALU_q3, ALU_q4, ALU_q5, ALU_q6, ALU_q7, 1'b1, 1'b0, _74541_1_p13, _74541_1_p14, _74541_1_p15, _74541_1_p16, _74541_1_p17, _74541_1_p18, _74541_1_p19, _74541_1_p20
  PullDown pulldown_1 (.out(_74541_1_p13));
  PullDown pulldown_2 (.out(_74541_1_p14));
  not not_18 (ALU_A, FLAG_CLOCK);
  PullDown pulldown_3 (.out(_74541_1_p15));
  PullDown pulldown_4 (.out(_74541_1_p16));
  PullDown pulldown_5 (.out(_74541_1_p17));
  PullDown pulldown_6 (.out(_74541_1_p18));
  Stack_FOR_MIT stack_for_mit_1 (
    .D0(A0), .D1(A1), .D2(A2), .D3(A3), .D4(A4), .D5(A5), .D6(A6), .D7(A7), .Clock(CLK_STACK_AU),
    .nPUSH_POP_A(nPUSH_POP_AU), .Q0(D0), .Q1(D1), .Q2(D2), .Q3(D3), .Q4(D4), .Q5(D5), .Q6(D6), .Q7(D7));
  Stack_FOR_MIT stack_for_mit_2 (
    .D0(A8), .D1(A9), .D2(A10), .D3(A11), .D4(A12), .D5(A13), .D6(A14), .D7(A15), .Clock(CLK_STACK_AD),
    .nPUSH_POP_A(nPUSH_POP_AD), .Q0(D0), .Q1(D1), .Q2(D2), .Q3(D3), .Q4(D4), .Q5(D5), .Q6(D6), .Q7(D7));
  PullDown pulldown_7 (.out(_74541_1_p19));
  PullDown pulldown_8 (.out(_74541_1_p20));
  // _74245 _74245_1: pin names not known; wires that end beside it: O_nI, F_I_O, 1'b1, D0, 1'b0, D1, _74245_1_p7, D2, _74245_1_p9, D3, _74245_1_p11
  // _74374 F: pin names not known; wires that end beside it: nDISPLAYFG, D0, D1, D2, D3, D4, D5, D6, D7, F_LD, 1'b1, _74245_1_p7, _74245_1_p9, _74245_1_p11, F_p15, F_p16, F_p17, F_p18, F_p19
  // _74374 G: pin names not known; wires that end beside it: 1'b0, nDISPLAYFG, D0, D1, D2, D3, D4, D5, D6, D7, G_LD, 1'b1, 1'b0, G_p14, G_p15, G_p16, G_p17, G_p18, G_p19, G_p20, G_p21
  // _74374 PC_BUFFER: pin names not known; wires that end beside it: 1'b0, D0, D1, D2, D3, D4, D5, D6, D7, ADR_BYTE1, 1'b1, 1'b0, PC_BUFFER_p13, PC_BUFFER_p14, PC_BUFFER_p15, PC_BUFFER_p16, PC_BUFFER_p17, PC_BUFFER_p18, PC_BUFFER_p19, PC_BUFFER_p20
  // _74374 PC_BUFFER_2: pin names not known; wires that end beside it: 1'b0, D0, D1, D2, D3, D4, D5, D6, D7, ADR_BYTE2, 1'b1, 1'b0, PC_BUFFER_2_p13, PC_BUFFER_2_p14, PC_BUFFER_2_p15, PC_BUFFER_2_p16, PC_BUFFER_2_p17, PC_BUFFER_2_p18, PC_BUFFER_2_p19, PC_BUFFER_2_p20
  // _74245 _74245_2: pin names not known; wires that end beside it: D4, F_p15, D5, F_p16, D6, F_p17, D7, F_p18, F_p19, O_nI, G_I_O, 1'b1, D0, 1'b0, D1, G_p14, D2, G_p15, D3, G_p16, D4, G_p17, D5, G_p18, D6, G_p19, D7, G_p20, G_p21
  and and_9 (and_9_out, JMP_FC, JMP);
  // _74161 _74161_1: pin names not known; wires that end beside it: PC_BUFFER_p13, PC_BUFFER_p14, PC_BUFFER_p15, PC_BUFFER_p16, and_9_out, CLK, 1'b1, 1'b1, 1'b1, 1'b0, reset, _74161_1_p12, _74161_1_p13, _74161_1_p14, _74161_1_p15, _74161_1_p16
  // _74161 _74161_2: pin names not known; wires that end beside it: PC_BUFFER_p17, PC_BUFFER_p18, PC_BUFFER_p19, PC_BUFFER_p20, and_9_out, CLK, _74161_1_p16, 1'b1, 1'b1, 1'b0, reset, _74161_2_p12, _74161_2_p13, _74161_2_p14, _74161_2_p15, _74161_2_p16
  // _74161 _74161_3: pin names not known; wires that end beside it: PC_BUFFER_2_p13, PC_BUFFER_2_p14, PC_BUFFER_2_p15, PC_BUFFER_2_p16, and_9_out, CLK, _74161_2_p16, 1'b1, 1'b1, 1'b0, reset, _74161_3_p12, _74161_3_p13, _74161_3_p14, _74161_3_p15, _74161_3_p16
  // _74161 _74161_4: pin names not known; wires that end beside it: PC_BUFFER_2_p17, PC_BUFFER_2_p18, PC_BUFFER_2_p19, PC_BUFFER_2_p20, and_9_out, CLK, _74161_3_p16, 1'b1, 1'b1, 1'b0, reset, _74161_4_p12, _74161_4_p13, _74161_4_p14, _74161_4_p15
  // _74541 _74541_5: pin names not known; wires that end beside it: nROM_RAM, nROM_RAM, _74161_1_p12, _74161_1_p13, _74161_1_p14, _74161_1_p15, _74161_2_p12, _74161_2_p13, _74161_2_p14, _74161_2_p15, 1'b1, 1'b0, A0, A1, A2, A3, A4, A5, A6, A7
  // _74541 _74541_6: pin names not known; wires that end beside it: nROM_RAM, nROM_RAM, _74161_3_p12, _74161_3_p13, _74161_3_p14, _74161_3_p15, _74161_4_p12, _74161_4_p13, _74161_4_p14, _74161_4_p15, 1'b1, 1'b0, A8, A9, A10, A11, A12, A13, A14, A15
  // _74373 _74373_1: pin names not known; wires that end beside it: 1'b1, 1'b0, 1'b0, _74245_1_p7, _74245_1_p9, _74245_1_p11, F_p15, F_p16, F_p17, F_p18, F_p19, _74373_1_p12, _74373_1_p13, _74373_1_p14, _74373_1_p15, _74373_1_p16, _74373_1_p17, _74373_1_p18, _74373_1_p19
  // _74373 _74373_2: pin names not known; wires that end beside it: TO_MEM, 1'b1, 1'b0, 1'b0, G_p14, G_p15, G_p16, G_p17, G_p18, G_p19, G_p20, G_p21, TO_MEM, _74373_2_p14, _74373_2_p15, _74373_2_p16, _74373_2_p17, _74373_2_p18, _74373_2_p19, _74373_2_p20, _74373_2_p21
  not not_19 (not_19_out, nROM_RAM);
  // _74541 _74541_7: pin names not known; wires that end beside it: not_19_out, not_19_out, _74373_1_p12, _74373_1_p13, _74373_1_p14, _74373_1_p15, _74373_1_p16, _74373_1_p17, _74373_1_p18, _74373_1_p19, 1'b1, 1'b0, A0, A1, A2, A3, A4, A5, A6, A7
  // _74541 _74541_8: pin names not known; wires that end beside it: not_19_out, not_19_out, _74373_2_p14, _74373_2_p15, _74373_2_p16, _74373_2_p17, _74373_2_p18, _74373_2_p19, _74373_2_p20, _74373_2_p21, 1'b1, 1'b0, A8, A9, A10, A11, A12, A13, A14, A15
  EEPROM #(.AddrBits(16), .Bits(8)) eeprom_1 (
    .A({A15, A14, A13, A12, A11, A10, A9, A8, A7, A6, A5, A4, A3, A2, A1, A0}), .CS(~nROM_RAM), .WE(~1'b1),
    .OE(~nROM_OE), .D(eeprom_1_d));
  nor nor_2 (nor_2_out, nROM_RAM, ~1'b1, nROM_OE);  // NOr
  not not_20 (not_20_out, nROM_RAM);
  BusSplitter #(.Bits(8)) bussplitter_1 (
    .D(eeprom_1_d), .OE(nor_2_out), .D0(D0), .D1(D1), .D2(D2), .D3(D3), .D4(D4), .D5(D5), .D6(D6), .D7(D7));
  // _74154 _74154_1: pin names not known; wires that end beside it: 1'b1, 1'b0, 1'b0, not_20_out, A12, A13, A14, A15, 1'b0, _74154_1_p10, _74154_1_p11
  EEPROM #(.AddrBits(12), .Bits(8)) eeprom_2 (
    .A({A11, A10, A9, A8, A7, A6, A5, A4, A3, A2, A1, A0}), .CS(~_74154_1_p10), .WE(~WE), .OE(~OE),
    .D(eeprom_2_d));
  nor nor_3 (nor_3_out, _74154_1_p10, ~WE, OE);  // NOr
  BusSplitter #(.Bits(8)) bussplitter_2 (
    .D(eeprom_2_d), .OE(nor_3_out), .D0(D0), .D1(D1), .D2(D2), .D3(D3), .D4(D4), .D5(D5), .D6(D6), .D7(D7));
  // _74154 _74154_2: pin names not known; wires that end beside it: 1'b1, 1'b0, 1'b0, _74154_1_p11, A0, A1, A2, A3, 1'b0, _74154_2_p10, _74154_2_p11
  // _74373 _74373_3: pin names not known; wires that end beside it: 1'b1, 1'b0, 1'b0, D0, D1, D2, D3, 1'b0, 1'b0, 1'b0, 1'b0, _74154_2_p10, _74373_3_p13, _74373_3_p14, _74373_3_p15, _74373_3_p16
  // _7448 _7448_1: pin names not known; wires that end beside it: 1'b1, 1'b0, _74373_3_p13, _74373_3_p14, _74373_3_p15, _74373_3_p16, 1'b0, 1'b0, 1'b0, _7448_1_p10, _7448_1_p11, _7448_1_p12, _7448_1_p13, _7448_1_p14, _7448_1_p15, _7448_1_p16
  Seven_Seg seven_seg_1 (
    .a(_7448_1_p10), .b(_7448_1_p11), .c(_7448_1_p12), .d(_7448_1_p13), .e(_7448_1_p14), .f(_7448_1_p15),
    .g(_7448_1_p16), .dp(1'b0));
  // _74373 _74373_4: pin names not known; wires that end beside it: 1'b1, 1'b0, 1'b0, D0, D1, D2, D3, 1'b0, 1'b0, 1'b0, 1'b0, _74154_2_p11, _74373_4_p13, _74373_4_p14, _74373_4_p15, _74373_4_p16
  // _7448 _7448_2: pin names not known; wires that end beside it: 1'b1, 1'b0, _74373_4_p13, _74373_4_p14, _74373_4_p15, _74373_4_p16, 1'b0, 1'b0, 1'b0, _7448_2_p10, _7448_2_p11, _7448_2_p12, _7448_2_p13, _7448_2_p14, _7448_2_p15, _7448_2_p16
  Seven_Seg seven_seg_2 (
    .a(_7448_2_p10), .b(_7448_2_p11), .c(_7448_2_p12), .d(_7448_2_p13), .e(_7448_2_p14), .f(_7448_2_p15),
    .g(_7448_2_p16), .dp(1'b0));

  // Notes on the sheet:
  //   clock_IN: Hz: 50
  //   INSTRUCTION DECODER
  //   REGISTERS
  //   ALU
  //   contents of INSTRUCTION_DECODER (hex, n*v repeats v):
  //   10000002,15*0,10000002,200,14,13*0,10000002,10,800,10,400,2000014
  //   ,10*0,10000002,18,40,14,12*0,10000002,8080000,8080400,4080000
  //   ,4080800,2000014,10*0,10000002,8080000,8080400,4080000,4080800
  //   ,10,a000,2000014,8*0,10000002,8,10,388080000,10,384080000,90000
  //   ,90040,14,7*0,10000002,8,2080000,2080040,14,11*0,10000002,8,80300
  //   ,14,12*0,10000002,8,10,388080000,10,384080000,90000,90040,14,7*0
  //   ,10000002,8,2080000,2080040,14,11*0,10000002,18,40,14,12*0,10000002
  //   ,81000,83000,83400,84000,8c000,8c800,2000014,8*0,10000002,15*0
  //   ,10000002,15*0,10000002,15*0,10000002,8,80380,14,12*0,10000002
  //   ,8,10,388080000,10,384080000,90000,90040,14,7*0,10000002,8,2080000
  //   ,2080040,14,11*0,10000002,18,40,14,12*0,10000002,15*0,10000002
  //   ,15*0,10000002,15*0,10000002,15*0,10000002,15*0,10000002,8,10
  //   ,388080000,10,384080000,90000,90040,14,7*0,10000002,8,2080000
  //   ,2080040,14,11*0,10000002,18,40,14,12*0,10000002,15*0,10000002
  //   ,15*0,10000002,15*0,10000002,15*0,10000002,15*0,10000002,8,10
  //   ,388080000,10,384080000,90000,90040,14,7*0,10000002,8,2080000
  //   ,2080040,14,11*0,10000002,18,40,14,12*0,10000002,15*0,10000002
  //   ,15*0,10000002,15*0,10000002,15*0,10000002,15*0,10000002,8,10
  //   ,388080000,10,384080000,90000,90040,14,7*0,10000002,8,2080000
  //   ,2080040,14,11*0,10000002,18,40,14,12*0,10000002,15*0,10000002
  //   ,15*0,10000002,15*0,10000002,15*0,10000002,15*0,10000002,8,10
  //   ,388080000,10,384080000,90000,90040,14,7*0,10000002,8,20080000
  //   ,20080040,14,11*0,10000002,18,40,14,12*0,10000002,15*0,10000002
  //   ,15*0,10000002,15*0,10000002,15*0,10000002,15*0,10000002,15*0
  //   ,10000002,15*0,10000002,10,100000,250000,14,11*0,10000002,15*0
  //   ,10000002,15*0,10000002,15*0,10000002,15*0,10000002,8,80060,14
  //   ,12*0,10000002,8,80060,14,12*0,10000002,8,80060,14,12*0,10000002
  //   ,8,80060,14,12*0,10000002,8,80060,14,12*0,10000002,8,8080060,14
  //   ,12*0,10000002,8,4080060,14,12*0,10000002,8,30000,30040,14,11*0
  //   ,10000002,8,80060,14,12*0,10000002,8,80060,14,12*0,10000002,8
  //   ,80060,14,12*0,10000002,8,80060,14,12*0,10000002,8,80060,14,12*0
  //   ,10000002,8,8080060,14,12*0,10000002,8,4080060,14,12*0,10000002
  //   ,8,30000,30040,14,11*0,10000002,8,80060,14,12*0,10000002,8,80060
  //   ,14,12*0,10000002,8,80060,14,12*0,10000002,8,80060,14,12*0,10000002
  //   ,8,80060,14,12*0,10000002,8,8080060,14,12*0,10000002,8,4080060
  //   ,14,12*0,10000002,8,30000,30040,14,11*0,10000002,8,80060,14,12*0
  //   ,10000002,8,80060,14,12*0,10000002,8,80060,14,12*0,10000002,8
  //   ,80060,14,12*0,10000002,8,80060,14,12*0,10000002,8,8080060,14
  //   ,12*0,10000002,8,4080060,14,12*0,10000002,8,30000,30040,14,11*0
  //   ,10000002,8,80060,14,12*0,10000002,8,80060,14,12*0,10000002,8
  //   ,80060,14,12*0,10000002,8,80060,14,12*0,10000002,8,80060,14,12*0
  //   ,10000002,8,8080060,14,12*0,10000002,8,4080060,14,12*0,10000002
  //   ,8,30000,30040,14,11*0,10000002,8,80060,14,12*0,10000002,8,80060
  //   ,14,12*0,10000002,8,80060,14,12*0,10000002,8,80060,14,12*0,10000002
  //   ,8,80060,14,12*0,10000002,8,8080060,14,12*0,10000002,8,4080060
  //   ,14,12*0,10000002,8,30000,30040,14,11*0,10000002,8,80060,14,12*0
  //   ,10000002,8,80060,14,12*0,10000002,8,80060,14,12*0,10000002,8
  //   ,80060,14,12*0,10000002,8,80060,14,12*0,10000002,8,8080060,14
  //   ,12*0,10000002,8,4080060,14,12*0,10000002,8,30000,30040,14,11*0
  //   ,10000002,8,80020,d0020,14,11*0,10000002,8,80020,d0020,14,11*0
  //   ,10000002,8,80020,d0020,14,11*0,10000002,8,80020,d0020,14,11*0
  //   ,10000002,8,80020,d0020,14,11*0,10000002,8,8080020,d0020,14,11*0
  //   ,10000002,8,4080020,d0020,14,11*0,10000002,8,30000,30040,14,11*0
  //   ,10000002,180,14,13*0,10000002,8,80020,801a0,14,11*0,10000002
  //   ,8,80020,801a0,14,11*0,10000002,8,80020,801a0,14,11*0,10000002
  //   ,8,80020,801a0,14,11*0,10000002,8,80020,801a0,14,11*0,10000002
  //   ,8,80020,801a0,14,11*0,10000002,30000,30180,14,12*0,10000002,400180
  //   ,14,13*0,10000002,8,80020,4801a0,14,11*0,10000002,8,80020,4801a0
  //   ,14,11*0,10000002,8,80020,4801a0,14,11*0,10000002,8,80020,4801a0
  //   ,14,11*0,10000002,8,80020,4801a0,14,11*0,10000002,8,80020,4801a0
  //   ,14,11*0,10000002,30000,430180,14,12*0,10000002,1000100,14,13*0
  //   ,10000002,8,80020,1080120,14,11*0,10000002,8,80020,1080120,14
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  //   STACK
  //   PC
  //   OUTSIDE
  //   contents of eeprom_1 (hex, n*v repeats v):
  //   2b,8,33,0,5,40,0,0,6
  //   contents of eeprom_2 (hex, n*v repeats v):
  //   93,4f,7e,1f,9,16,68,5*0,94,52*0,1,638*0,8,396*0,a6,191*0,f0,57*0
  //   ,e6,185*0,9,16*0,1,173*0,80,12*0,61,254*0,c6,139*0,42,94*0,57
  //   ,1162*0,c7,94*0,14,189*0,66,82*0,ca,101*0,e0,73*0,20
endmodule
