// Digital circuit ALU_V2.dig as structural Verilog
module ALU_V2 (
  input  IN0,
  input  CARRY_in,
  input  S_1,
  input  S_2,
  input  S_3,
  input  IN1,
  input  IN2,
  input  IN3,
  input  IN4,
  input  IN5,
  input  IN6,
  input  IN7,
  input  IN8,
  input  IN9,
  input  IN10,
  input  IN11,
  input  IN12,
  input  IN13,
  input  IN14,
  input  IN15,
  output CARRY_FLAG,
  output O_FLAG,
  output CLOCK,
  output Q0,
  output Q1,
  output Q2,
  output Q3,
  output Q4,
  output Q5,
  output Q6,
  output Q7,
  output gt,
  output eq,
  output lt,
  output P_FLAG
);

  wire _74138_1_p9, _74138_1_p10, _74138_1_p11, _74138_1_p12, _74138_1_p13, _74138_1_p14, _74138_1_p15,
       _74374_1_p10, _74374_2_p13, _74374_2_p14, _74374_2_p15, _74374_2_p16, _74374_2_p17, _74374_2_p18,
       _74374_2_p19, _74374_2_p20, _74541_1_p13, _74541_1_p14, _74541_1_p15, _74541_1_p16, _74541_1_p17,
       _74541_1_p18, _74541_1_p19, _74541_1_p20, and_9_out, and_10_out, and_11_out, and_12_out, and_13_out,
       and_14_out, and_15_out, and_16_out, and_17_out, and_18_out, and_19_out, and_20_out, and_21_out,
       and_22_out, and_23_out, and_24_out, not_1_out, not_2_out, not_3_out, not_4_out, not_5_out, or_10_out,
       or_11_out, or_12_out, or_13_out, or_14_out, or_15_out, or_16_out, or_17_out, or_20_out, xor_1_out,
       xor_2_out, xor_3_out, xor_4_out, xor_5_out, xor_6_out, xor_7_out, xor_8_out, xor_9_out, xor_10_out,
       xor_11_out, xor_12_out, xor_13_out, xor_14_out, xor_15_out, xor_16_out;
  wire [6:6] _74374_1_p20;
  wire [7:0] _74374_1_p15, and_1_out, or_2_out, xor_17_out;

  // _74280 _74280_1: pin names not known; wires that end beside it: 1'b1, 1'b0, IN0, IN1, IN2, IN3, IN4, IN5, IN6, IN7, 1'b0, P_FLAG
  // _74374 _74374_1: pin names not known; wires that end beside it: 1'b0, IN0, IN1, IN2, IN3, IN4, IN5, IN6, IN7, _74374_1_p10, 1'b1, 1'b0, _74374_1_p15[1], _74374_1_p15[2], _74374_1_p15[3], _74374_1_p15[4], _74374_1_p15[5], _74374_1_p15[6], _74374_1_p15[7], _74374_1_p20[6]
  // _74374 _74374_2: pin names not known; wires that end beside it: 1'b0, IN8, IN9, IN10, IN11, IN12, IN13, IN14, IN15, _74374_1_p10, 1'b1, 1'b0, _74374_2_p13, _74374_2_p14, _74374_2_p15, _74374_2_p16, _74374_2_p17, _74374_2_p18, _74374_2_p19, _74374_2_p20
  // _74138 _74138_1: pin names not known; wires that end beside it: 1'b1, 1'b0, 1'b1, 1'b0, 1'b0, S_1, S_2, S_3, _74138_1_p9, _74138_1_p10, _74138_1_p11, _74138_1_p12, _74138_1_p13, _74138_1_p14, _74138_1_p15
  not not_1 (not_1_out, _74138_1_p9);
  not not_2 (not_2_out, _74138_1_p10);
  not not_3 (not_3_out, _74138_1_p11);
  not not_4 (not_4_out, _74138_1_p12);
  not not_5 (not_5_out, _74138_1_p13);
  // _74682 _74682_1: pin names not known; wires that end beside it: _74374_1_p15[1], _74374_1_p15[2], _74374_1_p15[3], _74374_1_p15[4], _74374_1_p15[5], _74374_1_p15[6], _74374_1_p15[7], _74374_1_p20[6], _74374_2_p13, _74374_2_p14, _74374_2_p15, _74374_2_p16, _74374_2_p17, _74374_2_p18, _74374_2_p19, _74374_2_p20, 1'b1, 1'b0, gt, eq
  nand nand_1 (lt, gt, eq);
  or or_1 (_74374_1_p10, not_1_out, not_2_out, not_3_out, not_4_out, not_5_out);
  and and_1 (and_1_out[0], _74374_1_p15[1], _74374_2_p13);
  and and_2 (and_1_out[1], _74374_1_p15[2], _74374_2_p14);
  and and_3 (and_1_out[2], _74374_1_p15[3], _74374_2_p15);
  and and_4 (and_1_out[3], _74374_1_p15[4], _74374_2_p16);
  and and_5 (and_1_out[4], _74374_1_p15[5], _74374_2_p17);
  and and_6 (and_1_out[5], _74374_1_p15[6], _74374_2_p18);
  and and_7 (and_1_out[6], _74374_1_p15[7], _74374_2_p19);
  and and_8 (and_1_out[7], _74374_1_p20[6], _74374_2_p20);
  or or_2 (or_2_out[0], _74374_1_p15[1], _74374_2_p13);
  or or_3 (or_2_out[1], _74374_1_p15[2], _74374_2_p14);
  or or_4 (or_2_out[2], _74374_1_p15[3], _74374_2_p15);
  or or_5 (or_2_out[3], _74374_1_p15[4], _74374_2_p16);
  or or_6 (or_2_out[4], _74374_1_p15[5], _74374_2_p17);
  or or_7 (or_2_out[5], _74374_1_p15[6], _74374_2_p18);
  or or_8 (or_2_out[6], _74374_1_p15[7], _74374_2_p19);
  or or_9 (or_2_out[7], _74374_1_p20[6], _74374_2_p20);
  // _74541 _74541_1: pin names not known; wires that end beside it: 1'b1, 1'b0, not_1_out, not_1_out, _74374_2_p13, _74374_2_p14, _74374_2_p15, _74374_2_p16, _74374_2_p17, _74374_2_p18, _74374_2_p19, _74374_2_p20, _74541_1_p13, _74541_1_p14, _74541_1_p15, _74541_1_p16, _74541_1_p17, _74541_1_p18, _74541_1_p19, _74541_1_p20
  PullDown pulldown_1 (.out(_74541_1_p20));
  PullDown pulldown_2 (.out(_74374_1_p15[0]));
  Delay #(.delayTime(4)) delay_1 (.in(_74374_1_p10), .out(CLOCK));
  PullDown pulldown_3 (.out(_74541_1_p19));
  PullDown pulldown_4 (.out(_74541_1_p18));
  PullDown pulldown_5 (.out(_74541_1_p17));
  PullDown pulldown_6 (.out(_74541_1_p16));
  PullDown pulldown_7 (.out(_74541_1_p15));
  PullDown pulldown_8 (.out(_74541_1_p14));
  PullDown pulldown_9 (.out(_74541_1_p13));
  assign {Q7, Q6, Q5, Q4, Q3, Q2, Q1, Q0} = not_4_out ? and_1_out : 8'bz;  // Driver driver_1
  assign {Q7, Q6, Q5, Q4, Q3, Q2, Q1, Q0} = not_5_out ? or_2_out : 8'bz;  // Driver driver_2
  assign {Q7, Q6, Q5, Q4, Q3, Q2, Q1, Q0} = ~_74138_1_p14 ? _74374_1_p15 : 8'bz;  // DriverInvSel driverinvsel_1
  assign {Q7, Q6, Q5, Q4, Q3, Q2, Q1, Q0} = ~_74138_1_p15 ? {_74374_1_p15[0], _74374_1_p20[6], _74374_1_p15[7:2]} : 8'bz;  // DriverInvSel driverinvsel_2
  or or_10 (or_10_out, not_1_out, not_2_out);
  xor xor_1 (xor_1_out, or_10_out, _74374_1_p15[1]);
  xor xor_2 (xor_2_out, or_10_out, _74374_1_p15[2]);
  xor xor_3 (xor_3_out, or_10_out, _74374_1_p15[3]);
  xor xor_4 (xor_4_out, or_10_out, _74374_1_p15[4]);
  xor xor_5 (xor_5_out, or_10_out, _74374_1_p15[5]);
  xor xor_6 (xor_6_out, or_10_out, _74374_1_p15[6]);
  xor xor_7 (xor_7_out, or_10_out, _74374_1_p15[7]);
  xor xor_8 (xor_8_out, or_10_out, _74374_1_p20[6]);
  or or_11 (or_11_out, CARRY_in, not_2_out);
  xor xor_9 (xor_9_out, xor_1_out, _74541_1_p20);
  and and_9 (and_9_out, xor_1_out, _74541_1_p20);
  xor xor_10 (xor_10_out, xor_2_out, _74541_1_p19);
  and and_10 (and_10_out, xor_2_out, _74541_1_p19);
  xor xor_11 (xor_11_out, xor_3_out, _74541_1_p18);
  and and_11 (and_11_out, xor_3_out, _74541_1_p18);
  xor xor_12 (xor_12_out, xor_4_out, _74541_1_p17);
  and and_12 (and_12_out, xor_4_out, _74541_1_p17);
  xor xor_13 (xor_13_out, xor_5_out, _74541_1_p16);
  and and_13 (and_13_out, xor_5_out, _74541_1_p16);
  xor xor_14 (xor_14_out, xor_6_out, _74541_1_p15);
  and and_14 (and_14_out, xor_6_out, _74541_1_p15);
  xor xor_15 (xor_15_out, xor_7_out, _74541_1_p14);
  and and_15 (and_15_out, xor_7_out, _74541_1_p14);
  xor xor_16 (xor_16_out, xor_8_out, _74541_1_p13);
  and and_16 (and_16_out, xor_8_out, _74541_1_p13);
  xor xor_17 (xor_17_out[0], or_11_out, xor_9_out);
  and and_17 (and_17_out, or_11_out, xor_9_out);
  PullDown pulldown_10 (.out(or_11_out));
  xor xor_18 (xor_17_out[1], or_12_out, xor_10_out);
  and and_18 (and_18_out, or_12_out, xor_10_out);
  xor xor_19 (xor_17_out[2], or_13_out, xor_11_out);
  and and_19 (and_19_out, or_13_out, xor_11_out);
  xor xor_20 (xor_17_out[3], or_14_out, xor_12_out);
  and and_20 (and_20_out, or_14_out, xor_12_out);
  xor xor_21 (xor_17_out[4], or_15_out, xor_13_out);
  and and_21 (and_21_out, or_15_out, xor_13_out);
  xor xor_22 (xor_17_out[5], or_16_out, xor_14_out);
  and and_22 (and_22_out, or_16_out, xor_14_out);
  xor xor_23 (xor_17_out[6], or_17_out, xor_15_out);
  and and_23 (and_23_out, or_17_out, xor_15_out);
  xor xor_24 (xor_17_out[7], O_FLAG, xor_16_out);
  and and_24 (and_24_out, O_FLAG, xor_16_out);
  or or_12 (or_12_out, and_17_out, and_9_out);
  or or_13 (or_13_out, and_18_out, and_10_out);
  or or_14 (or_14_out, and_19_out, and_11_out);
  or or_15 (or_15_out, and_20_out, and_12_out);
  or or_16 (or_16_out, and_21_out, and_13_out);
  or or_17 (or_17_out, and_22_out, and_14_out);
  or or_18 (O_FLAG, and_23_out, and_15_out);
  or or_19 (CARRY_FLAG, and_24_out, and_16_out);
  or or_20 (or_20_out, not_1_out, not_2_out, not_3_out);
  assign {Q7, Q6, Q5, Q4, Q3, Q2, Q1, Q0} = or_20_out ? xor_17_out : 8'bz;  // Driver driver_3

  // Notes on the sheet:
  //   O_FLAG: When there is an overflow from bit 6 - bit 7
endmodule
