// Digital circuit Stack_FOR_MIT.dig as structural Verilog
module Stack_FOR_MIT (
  input  D0,
  input  D1,
  input  D2,
  input  D3,
  input  Clock,
  input  nPUSH_POP_A,
  input  D4,
  input  D5,
  input  D6,
  input  D7,
  output Q0,
  output Q1,
  output Q2,
  output Q3,
  output Q4,
  output Q5,
  output Q6,
  output Q7
);

  wire _74189_1_p13, _74189_1_p14, _74189_1_p15, _74189_1_p16, _74189_2_p13, _74189_2_p14, _74189_2_p15,
       _74189_2_p16, _74191_1_p11, _74191_1_p12, _74191_1_p13, _74191_1_p14, not_1_out, not_2_out, not_3_out,
       not_4_out, not_5_out, not_6_out, not_7_out, not_8_out;

  // _74191 _74191_1: pin names not known; wires that end beside it: 1'b0, 1'b0, 1'b0, 1'b0, 1'b1, 1'b0, 1'b1, nPUSH_POP_A, 1'b0, Clock, _74191_1_p11, _74191_1_p12, _74191_1_p13, _74191_1_p14
  // _74189 _74189_1: pin names not known; wires that end beside it: _74191_1_p11, _74191_1_p12, _74191_1_p13, _74191_1_p14, D0, D1, D2, D3, nPUSH_POP_A, 1'b0, 1'b1, 1'b0, _74189_1_p13, _74189_1_p14, _74189_1_p15, _74189_1_p16
  // _74189 _74189_2: pin names not known; wires that end beside it: _74191_1_p11, _74191_1_p12, _74191_1_p13, _74191_1_p14, D4, D5, D6, D7, nPUSH_POP_A, 1'b0, 1'b1, 1'b0, _74189_2_p13, _74189_2_p14, _74189_2_p15, _74189_2_p16
  not not_1 (not_1_out, _74189_1_p13);
  not not_2 (not_2_out, _74189_1_p14);
  not not_3 (not_3_out, _74189_1_p15);
  not not_4 (not_4_out, _74189_1_p16);
  not not_5 (not_5_out, _74189_2_p13);
  not not_6 (not_6_out, _74189_2_p14);
  not not_7 (not_7_out, _74189_2_p15);
  not not_8 (not_8_out, _74189_2_p16);
  assign Q0 = nPUSH_POP_A ? not_1_out : 1'bz;  // Driver driver_1
  assign Q1 = nPUSH_POP_A ? not_2_out : 1'bz;  // Driver driver_2
  assign Q2 = nPUSH_POP_A ? not_3_out : 1'bz;  // Driver driver_3
  assign Q3 = nPUSH_POP_A ? not_4_out : 1'bz;  // Driver driver_4
  assign Q4 = nPUSH_POP_A ? not_5_out : 1'bz;  // Driver driver_5
  assign Q5 = nPUSH_POP_A ? not_6_out : 1'bz;  // Driver driver_6
  assign Q6 = nPUSH_POP_A ? not_7_out : 1'bz;  // Driver driver_7
  assign Q7 = nPUSH_POP_A ? not_8_out : 1'bz;  // Driver driver_8
endmodule
